// Logisim project Пример схемы АЛУ.circ as structural Verilog: 2 circuits, main circuit main
module main (
  input  [7:0] in_1,
  input  [7:0] in_2,
  input  [3:0] in_3,
  output [7:0] out_4
);

  Hex_Digit_Display hex_digit_display_1 (.value(in_1[3:0]));  // open: dp
  Hex_Digit_Display hex_digit_display_2 (.value(in_1[7:4]));  // open: dp
  Hex_Digit_Display hex_digit_display_3 (.value(in_2[3:0]));  // open: dp
  Hex_Digit_Display hex_digit_display_4 (.value(in_2[7:4]));  // open: dp
  Hex_Digit_Display hex_digit_display_5 (.value(out_4[7:4]));  // open: dp
  \АЛУ  \u_АЛУ  (.\А (in_1), .B(in_2), .OC(in_3), .C(out_4));
  Hex_Digit_Display hex_digit_display_6 (.value(out_4[3:0]));  // open: dp
endmodule

module \АЛУ  (
  input  [7:0] \А ,
  input  [7:0] B,
  input  [3:0] OC,
  output [7:0] C
);

  wire [7:0] _0, _1, _2, _3, _4, _5, _6, _7, _8, _9, _10;

  assign _7 = ~\А ;  // NOT_Gate not_1, 8 bits wide
  assign _0 = ~(\А  | B);  // NOR_Gate _0, 8 bits wide
  Divider divider_1 (.a(\А ), .b(B), .out(_1));  // open: upper, rem
  assign _8 = \А  ^ B;  // XOR_Gate xor_1, 8 bits wide
  Adder adder_1 (.a(\А ), .b(B), .out(_2));  // open: cin, cout
  Shifter #(.shift("rl")) shifter_1 (.in(\А ), .\dist (B[2:0]), .out(_9));
  Multiplier multiplier_1 (.a(\А ), .b(B), .out(_3));  // open: cin, cout
  Multiplexer #(.select(4), .width(8), .enable("false")) multiplexer_1 (
    .in0(_0), .in1(_1), .in2(_2), .in3(_3), .in4(_4), .in5(_5), .in6(_6), .in7(_7), .in8(_8), .in9(_9),
    .in10(_10), .out(C), .sel(OC));  // open: in11, in12, in13, in14, in15
  Shifter #(.shift("rr")) shifter_2 (.in(\А ), .\dist (B[2:0]), .out(_10));
  Subtractor subtractor_1 (.a(\А ), .b(B), .out(_4));  // open: bin, bout
  assign _5 = \А  & B;  // AND_Gate and_1, 8 bits wide
  assign _6 = \А  | B;  // OR_Gate or_1, 8 bits wide

  // Other names for the same wires on the sheet: A[7:0] = \А 

  // Notes on the sheet:
  //   0
  //   1
  //   2
  //   3
endmodule
